# Fritzing sketch weather-station (saved by Fritzing 0.9.9b)
circuit board: 8.46667cm x 5.64444cm
breadboards: 1

parts:
  M1 = ESP32-C3-DevKitM-1 [part_number=ESP32-C3-DevKitM-1]
  DS1 = DS18B20 1-Wire Temperature Sensor [part_number=DS18B20]
  10k = Resistor [tolerance=±5% power=0.25 resistance=220 package=THT]
  33k = Resistor [tolerance=±5% power=0.25 resistance=220 package=THT]
  100k = Resistor [tolerance=±5% power=0.25 resistance=220 package=THT]
  10pF = Capacitor [package=cap-pth-small2]
  D1 = SOLAR-IXYS [package=solarbit-12x1]
  Part1 = Sunny Buddy MPPT LiPo Charger
  Rain_Count = RJ11 Jack [package=rj11-6]
  Anemometer_/_weathervane = RJ11 Jack [package=rj11-6]
  Part2 = Altitude/Pressure Sensor - MPL3115A2 Breakout [part_number=SEN-11084]
  AM1 = AM2320 Humidity and Temperature Sensor [part_number="Adafruit #3721"]

nets:
  GND: M1.GND-1, M1.GND-4, M1.GND-9, M1.GND-12, M1.GND-15, M1.GND-16, M1.GND-21, M1.GND-23, M1.GND-27, M1.GND-30, DS1.GND, 10k.Pin_1, 10pF.2, Part1.Load_-_(.1"_Header), Rain_Count.4, Anemometer_/_weathervane.5, Part2.GND, AM1.GND
  N1: M1.19, DS1.DQ
  N2: M1.4, 33k.Pin_1, Anemometer_/_weathervane.2
  N3: M1.5, 100k.Pin_1, 10pF.1, Rain_Count.3
  N4: M1.6, 10k.Pin_0, Anemometer_/_weathervane.3
  VDD: M1.3V3-17, M1.3V3-18, DS1.VDD, 33k.Pin_0, 100k.Pin_0, Part1.Load_+_(.1"_Header), Anemometer_/_weathervane.4, AM1.VDD
  N5: M1.2, Part2.SDA, AM1.SDA
  N6: M1.3, Part2.SCL, AM1.SCL
  N7: M1.5V-28, M1.5V-29
  N8: D1.A, Part1.Main_-
  N9: D1.C, Part1.Main_+

custom parts:
  ESP32-C3-DevKitM-1: The DOIT Esp32 DevKit v1 is one of the development board created by DOIT to evaluate the ESP-WROOM-32 module. It is based on the ESP32 microcontroller that boasts Wifi, Bluetooth, Ethernet and Low Power support all in a single chip. (vanepp) Feb 2021: converted to ESP32-C3-DevKitM-1. This chip is 30pins long (2 x15) and 11 pins width.
  Sunny Buddy MPPT LiPo Charger: Switch-mode MPPT charger for single cell LiPo batteries. Accepts up to 20V solar cell input.
  AM2320 Humidity and Temperature Sensor: AM2320 I2C Humidity and Temperature Sensor
